# Fritzing sketch leszek (saved by Fritzing 0.9.3b)

parts:
  Part1 = Arduino Pro Mini v13
  U2 = LCD-16X2 [package=lcd-16x2_noholes]
  R1 = Trimmer Potentiometer [maximum_resistance=10kΩ package=THT]
  R2 = Resistor [tolerance=±5% resistance=220 package="0805 [SMD]"]
  U3 = microSD Socket [package=micro-sd-socket-pp]
  Part2 = Real Time Clock Module - DS1307 RTC Breakout Board
  Part3 = ACS712 Low Current Sensor Board v12
  U4 = HALL-EFFECT [package=sc70]
  IC1 = Voltage Regulator [package=78xxl]
  C1 = Electrolytic Capacitor [capacitance=1µF package="100 mil [THT, electrolytic]"]  # not connected
  Power_plug1 = Power plug
  J1 = screw terminal, 3 pins
  R3 = Resistor [tolerance=±5% resistance=100k package=THT]  # not connected
  R4 = Resistor [tolerance=±5% resistance=680k package=THT]
  R5 = Resistor [tolerance=±5% resistance=470k package=THT]
  C2 = Ceramic Capacitor [capacitance=100nF package="100 mil [THT, multilayer]"]

nets:
  VCC: Part1.VCC, U2.VDD, R1.leg2, R2.Pin_0, Part2.5V, U4.VCC, IC1.OUT
  GND: Part1.GND, U2.R_W, U2.K, R1.leg1, Part2.GND, IC1.GND, Power_plug1.GND, J1.pin1, C2.0
  N1: Part1.A4, Part2.SDA
  N2: Part1.A5, Part2.SCL
  N3: Part1.A1, R5.Pin_1
  N4: Part1.A0, Part3.VO
  N5: Part1.D13/SCK, U3.SCK
  N6: Part1.D12/MISO, U3.GND
  N7: Part1.D11_PWM/MOSI, U3.DO
  N8: Part1.D10_PWM/SS, U3.RSV
  N9: Part1.D9_PWM, U2.DB7
  N10: Part1.D8, U2.DB6
  N11: Part1.D7, U2.DB5
  N12: Part1.D6_PWM, U2.DB4
  N13: Part1.D5_PWM, U2.E, U2.DB0
  N14: Part1.D4, U2.RS
  N15: Part1.D2, U4.OUT
  N16: U2.VO, R1.wiper
  N17: U2.A, R2.Pin_1
  N18: U3.SHIELD, Part3.5V
  N19: IC1.IN, Power_plug1.VCC
  N20: J1.pin3, R4.Pin_0

notes:
  Dzielnik napięcia
  RTC - zegar czasu rzeczywistego
  Miernik prądu
  karta SD
  czunik Halla
  wyswietlacz LCD 16x2
